# Fritzing sketch SolarGuardn (saved by Fritzing 0.9.3b)
circuit board: 5.47cm x 5.64444cm
breadboards: 1

parts:
  J1 = Screw terminal - 2 pins [package=THT]
  U2 = NodeMCU V1.0
  C2 = Capacitor Polarized [package=cpol-radial-10uf-25v]
  Q1 = TRANSISTOR_NPN [package=to-92-ammo]
  R5 = Resistor [tolerance=±5% resistance=100 package=THT]
  BME280 = BME280 Breakout
  VCC = Battery block 9V
  R6_10KΩ = TRIMPOT [package=trimpot_pth_s3_lock]
  Moisture1 = FC-28 Soil Hygrometer Module - Probe
  J2 = Screw terminal - 2 pins [package=THT]

nets:
  N1: J1.pin1, U2.Vin, C2.+, VCC.+
  GND: J1.pin2, U2.GND, C2.-, BME280.GND, VCC.-, R6_10KΩ.CCW
  N2: U2.D1, BME280.3.3V
  N3: U2.D2, Q1.C, R5.Pin_1
  N4: U2.D5, BME280.SCK/SCL
  N5: U2.D6, BME280.SDI/SDA
  N6: U2.A0, Q1.E, R6_10KΩ.WIPER
  N7: Q1.B, Moisture1.POS, J2.pin1
  N8: R5.Pin_0, Moisture1.NEG, J2.pin2

notes:
  SOLAR CELL
  lipo battery
  yard light hack
  with 5V booster

custom parts:
  NodeMCU V1.0: ESP8266 based NodeMCU
  FC-28 Soil Hygrometer Module - Probe: The FC-28 is a soil hygrometer module that uses the Texas Instruments LM393 comparator chip to provide an analog measurement of soil humidity.
